# Fritzing sketch LedPcb (saved by Fritzing 0.9.3b)
circuit board: 5.15596cm x 4.53316cm
breadboards: 1

parts:
  J15 = shrouded pin header, 10 pins [form="♂ (shrouded male)"]
  J16 = female pin header, 3 pins [form="♀ (female)"]
  J17 = female pin header, 3 pins [form="♀ (female)"]
  J14 = shrouded pin header, 10 pins [form="♂ (shrouded male)"]

nets:
  N1: J15.pin3, J16.pin3, J14.pin3
  N2: J15.pin4, J16.pin1, J14.pin2
  N3: J15.pin5, J16.pin2, J14.pin1
  N4: J15.pin6, J17.pin3, J14.pin10
  N5: J15.pin7, J17.pin2, J14.pin9
  N6: J15.pin8, J17.pin1, J14.pin8

notes:
  -
  B
  G
  R
  +
